// Logisim project Contagem.circ as structural Verilog: 8 circuits, main circuit NumberLed
module main (
);

  wire button_1_out, button_2_out, button_3_out, contagem_1_ativo, contagem_1_hora, contagem_1_minuto,
       contagem_1_segundo, HorasDecimal_2_s, HorasDecimal_2_t, HorasDecimal_2_u, HorasDecimal_2_v,
       HorasDecimal_2_w, HorasDecimal_2_x, HorasDecimal_2_y, HorasDecimal_2_z, HorasDecimal_s,
       HorasDecimal_t, HorasDecimal_u, HorasDecimal_v, HorasDecimal_w, HorasDecimal_x, HorasDecimal_y,
       HorasDecimal_z, HorasNumeral_2_s, HorasNumeral_2_t, HorasNumeral_2_u, HorasNumeral_2_v,
       HorasNumeral_2_w, HorasNumeral_2_x, HorasNumeral_2_y, HorasNumeral_2_z, HorasNumeral_s,
       HorasNumeral_t, HorasNumeral_u, HorasNumeral_v, HorasNumeral_w, HorasNumeral_x, HorasNumeral_y,
       HorasNumeral_z, MinutosDecimal_s, MinutosDecimal_t, MinutosDecimal_u, MinutosDecimal_v,
       MinutosDecimal_w, MinutosDecimal_x, MinutosDecimal_y, MinutosDecimal_z, MinutosNumeral_s,
       MinutosNumeral_t, MinutosNumeral_u, MinutosNumeral_v, MinutosNumeral_w, MinutosNumeral_x,
       MinutosNumeral_y, MinutosNumeral_z, or_1_out, or_2_out, or_3_out, Pausar_out, Play_out, Zerar_out;
  wire [3:0] adiciona_1_saidaa, adiciona_1_saidab, adiciona_2_saidaa, adiciona_2_saidab, adiciona_3_saidaa,
       adiciona_3_saidab;
  wire [7:0] adiciona_1_saida_8bits, adiciona_2_saida_8bits, adiciona_3_saida_8bits;

  _7_Segment_Display u_7_segment_display_1 (
    .g(HorasDecimal_u), .f(HorasDecimal_z), .a(HorasDecimal_y), .b(HorasDecimal_x), .e(HorasDecimal_v),
    .d(HorasDecimal_w), .c(HorasDecimal_s), .dp(HorasDecimal_t));
  NumberLed HorasDecimal (
    .a(adiciona_1_saidaa[3]), .b(adiciona_1_saidaa[2]), .c(adiciona_1_saidaa[1]), .d(adiciona_1_saidaa[0]),
    .x(HorasDecimal_x), .y(HorasDecimal_y), .z(HorasDecimal_z), .u(HorasDecimal_u), .v(HorasDecimal_v),
    .w(HorasDecimal_w), .s(HorasDecimal_s), .t(HorasDecimal_t));
  or or_1 (or_1_out, button_1_out, contagem_1_hora);
  Button button_1 (.out(button_1_out));
  _7_Segment_Display u_7_segment_display_2 (
    .g(HorasNumeral_u), .f(HorasNumeral_z), .a(HorasNumeral_y), .b(HorasNumeral_x), .e(HorasNumeral_v),
    .d(HorasNumeral_w), .c(HorasNumeral_s), .dp(HorasNumeral_t));
  NumberLed HorasNumeral (
    .a(adiciona_1_saidab[3]), .b(adiciona_1_saidab[2]), .c(adiciona_1_saidab[1]), .d(adiciona_1_saidab[0]),
    .x(HorasNumeral_x), .y(HorasNumeral_y), .z(HorasNumeral_z), .u(HorasNumeral_u), .v(HorasNumeral_v),
    .w(HorasNumeral_w), .s(HorasNumeral_s), .t(HorasNumeral_t));
  Adiciona adiciona_1 (
    .Somar(or_1_out), .Ativador(contagem_1_ativo), .ValorMaximo(8'h18), .Zerar(Zerar_out),
    .Saida_8Bits(adiciona_1_saida_8bits), .SaidaA(adiciona_1_saidaa), .SaidaB(adiciona_1_saidab));
  NumberLed MinutosDecimal (
    .a(adiciona_2_saidaa[3]), .b(adiciona_2_saidaa[2]), .c(adiciona_2_saidaa[1]), .d(adiciona_2_saidaa[0]),
    .x(MinutosDecimal_x), .y(MinutosDecimal_y), .z(MinutosDecimal_z), .u(MinutosDecimal_u),
    .v(MinutosDecimal_v), .w(MinutosDecimal_w), .s(MinutosDecimal_s), .t(MinutosDecimal_t));
  Button Play (.out(Play_out));
  Button Pausar (.out(Pausar_out));
  _7_Segment_Display u_7_segment_display_3 (
    .g(MinutosDecimal_u), .f(MinutosDecimal_z), .a(MinutosDecimal_y), .b(MinutosDecimal_x),
    .e(MinutosDecimal_v), .d(MinutosDecimal_w), .c(MinutosDecimal_s), .dp(MinutosDecimal_t));
  NumberLed MinutosNumeral (
    .a(adiciona_2_saidab[3]), .b(adiciona_2_saidab[2]), .c(adiciona_2_saidab[1]), .d(adiciona_2_saidab[0]),
    .x(MinutosNumeral_x), .y(MinutosNumeral_y), .z(MinutosNumeral_z), .u(MinutosNumeral_u),
    .v(MinutosNumeral_v), .w(MinutosNumeral_w), .s(MinutosNumeral_s), .t(MinutosNumeral_t));
  Adiciona adiciona_2 (
    .Somar(or_2_out), .Ativador(contagem_1_ativo), .ValorMaximo(8'h3c), .Zerar(Zerar_out),
    .Saida_8Bits(adiciona_2_saida_8bits), .SaidaA(adiciona_2_saidaa), .SaidaB(adiciona_2_saidab));
  or or_2 (or_2_out, button_2_out, contagem_1_minuto);
  Button button_2 (.out(button_2_out));
  Contagem contagem_1 (
    .Play(Play_out), .Pause(Pausar_out), .Horas(adiciona_1_saida_8bits), .Minutos(adiciona_2_saida_8bits),
    .Segundos(adiciona_3_saida_8bits), .Ativo(contagem_1_ativo), .Hora(contagem_1_hora),
    .Minuto(contagem_1_minuto), .Segundo(contagem_1_segundo));
  _7_Segment_Display u_7_segment_display_4 (
    .g(MinutosNumeral_u), .f(MinutosNumeral_z), .a(MinutosNumeral_y), .b(MinutosNumeral_x),
    .e(MinutosNumeral_v), .d(MinutosNumeral_w), .c(MinutosNumeral_s), .dp(MinutosNumeral_t));
  _7_Segment_Display u_7_segment_display_5 (
    .g(HorasDecimal_2_u), .f(HorasDecimal_2_z), .a(HorasDecimal_2_y), .b(HorasDecimal_2_x),
    .e(HorasDecimal_2_v), .d(HorasDecimal_2_w), .c(HorasDecimal_2_s), .dp(HorasDecimal_2_t));
  NumberLed HorasDecimal_2 (
    .a(adiciona_3_saidaa[3]), .b(adiciona_3_saidaa[2]), .c(adiciona_3_saidaa[1]), .d(adiciona_3_saidaa[0]),
    .x(HorasDecimal_2_x), .y(HorasDecimal_2_y), .z(HorasDecimal_2_z), .u(HorasDecimal_2_u),
    .v(HorasDecimal_2_v), .w(HorasDecimal_2_w), .s(HorasDecimal_2_s), .t(HorasDecimal_2_t));
  or or_3 (or_3_out, button_3_out, contagem_1_segundo);
  Button button_3 (.out(button_3_out));
  _7_Segment_Display u_7_segment_display_6 (
    .g(HorasNumeral_2_u), .f(HorasNumeral_2_z), .a(HorasNumeral_2_y), .b(HorasNumeral_2_x),
    .e(HorasNumeral_2_v), .d(HorasNumeral_2_w), .c(HorasNumeral_2_s), .dp(HorasNumeral_2_t));
  NumberLed HorasNumeral_2 (
    .a(adiciona_3_saidab[3]), .b(adiciona_3_saidab[2]), .c(adiciona_3_saidab[1]), .d(adiciona_3_saidab[0]),
    .x(HorasNumeral_2_x), .y(HorasNumeral_2_y), .z(HorasNumeral_2_z), .u(HorasNumeral_2_u),
    .v(HorasNumeral_2_v), .w(HorasNumeral_2_w), .s(HorasNumeral_2_s), .t(HorasNumeral_2_t));
  Adiciona adiciona_3 (
    .Somar(or_3_out), .Ativador(contagem_1_ativo), .ValorMaximo(8'h3c), .Zerar(Zerar_out),
    .Saida_8Bits(adiciona_3_saida_8bits), .SaidaA(adiciona_3_saidaa), .SaidaB(adiciona_3_saidab));
  Button Zerar (.out(Zerar_out));

  // Notes on the sheet:
  //   :
  //   :
endmodule

module NumberLed (
  input  a,
  input  b,
  input  c,
  input  d,
  output x,
  output y,
  output z,
  output u,
  output v,
  output w,
  output s,
  output t
);

  wire and_1_out, and_2_out, and_3_out, and_4_out, and_5_out, and_6_out, and_7_out, and_8_out, and_9_out,
       and_10_out, and_11_out, and_12_out, and_13_out, and_14_out, and_15_out, and_16_out, and_17_out,
       and_18_out, and_19_out, and_20_out, and_21_out, and_22_out, and_23_out, and_24_out, and_25_out,
       and_26_out, and_27_out, and_28_out, not_1_out, not_2_out, not_3_out, not_4_out, not_5_out, not_6_out,
       not_7_out, not_8_out, not_9_out, not_10_out, not_11_out, not_12_out, not_13_out, not_14_out,
       not_15_out, not_16_out, not_17_out, not_18_out, not_19_out, not_20_out, not_21_out, not_22_out,
       not_23_out, not_24_out, not_25_out, not_26_out, not_27_out, not_28_out, not_29_out, not_30_out,
       not_31_out, not_32_out, not_33_out, not_34_out, not_35_out, not_36_out, not_37_out, not_38_out,
       not_39_out, not_40_out, not_41_out, not_42_out, not_43_out, not_44_out, not_45_out, not_46_out,
       not_47_out, not_48_out, not_49_out, not_50_out, not_51_out, not_52_out;

  not not_1 (not_1_out, a);
  and and_1 (and_1_out, not_1_out, not_2_out);
  not not_2 (not_2_out, b);
  not not_3 (not_3_out, a);
  and and_2 (and_2_out, not_3_out, not_4_out, not_5_out);
  not not_4 (not_4_out, c);
  not not_5 (not_5_out, d);
  not not_6 (not_6_out, b);
  and and_3 (and_3_out, not_6_out, not_7_out);
  not not_7 (not_7_out, c);
  not not_8 (not_8_out, a);
  and and_4 (and_4_out, not_8_out, c, d);
  not not_9 (not_9_out, a);
  and and_5 (and_5_out, not_9_out, not_10_out, not_11_out);
  not not_10 (not_10_out, b);
  not not_11 (not_11_out, d);
  not not_12 (not_12_out, a);
  and and_6 (and_6_out, not_12_out, c);
  not not_13 (not_13_out, a);
  and and_7 (and_7_out, not_13_out, b, d);
  and and_8 (and_8_out, a, not_14_out, not_15_out);
  not not_14 (not_14_out, b);
  not not_15 (not_15_out, c);
  not not_16 (not_16_out, a);
  not not_17 (not_17_out, c);
  and and_9 (and_9_out, not_16_out, not_17_out, not_18_out);
  not not_18 (not_18_out, d);
  not not_19 (not_19_out, a);
  and and_10 (and_10_out, not_19_out, b, not_20_out);
  not not_20 (not_20_out, c);
  not not_21 (not_21_out, a);
  and and_11 (and_11_out, not_21_out, b, not_22_out);
  not not_22 (not_22_out, d);
  and and_12 (and_12_out, a, not_23_out, not_24_out);
  not not_23 (not_23_out, b);
  not not_24 (not_24_out, c);
  not not_25 (not_25_out, a);
  not not_26 (not_26_out, b);
  and and_13 (and_13_out, not_25_out, not_26_out, c);
  not not_27 (not_27_out, a);
  and and_14 (and_14_out, not_27_out, b, not_28_out);
  not not_28 (not_28_out, c);
  not not_29 (not_29_out, a);
  and and_15 (and_15_out, not_29_out, b, not_30_out);
  not not_30 (not_30_out, d);
  and and_16 (and_16_out, a, not_31_out, not_32_out);
  not not_31 (not_31_out, b);
  not not_32 (not_32_out, c);
  not not_33 (not_33_out, b);
  not not_34 (not_34_out, c);
  and and_17 (and_17_out, not_33_out, not_34_out, not_35_out);
  not not_35 (not_35_out, d);
  not not_36 (not_36_out, a);
  and and_18 (and_18_out, not_36_out, c, not_37_out);
  not not_37 (not_37_out, d);
  not not_38 (not_38_out, a);
  not not_39 (not_39_out, b);
  not not_40 (not_40_out, d);
  not not_41 (not_41_out, a);
  not not_42 (not_42_out, b);
  not not_43 (not_43_out, a);
  not not_44 (not_44_out, d);
  not not_45 (not_45_out, a);
  not not_46 (not_46_out, c);
  not not_47 (not_47_out, b);
  not not_48 (not_48_out, c);
  not not_49 (not_49_out, b);
  and and_19 (and_19_out, not_49_out, not_50_out);
  not not_50 (not_50_out, c);
  not not_51 (not_51_out, a);
  and and_20 (and_20_out, not_51_out, d);
  not not_52 (not_52_out, a);
  and and_21 (and_21_out, not_52_out, b);
  and and_22 (and_22_out, a, c);
  and and_23 (and_23_out, a, b);
  or or_1 (x, and_1_out, and_2_out, and_3_out, and_4_out);
  or or_2 (y, and_5_out, and_6_out, and_7_out, and_8_out);
  or or_3 (z, and_9_out, and_10_out, and_11_out, and_12_out);
  or or_4 (u, and_13_out, and_14_out, and_15_out, and_16_out);
  or or_5 (v, and_17_out, and_18_out);
  and and_24 (and_24_out, not_38_out, not_39_out, not_40_out);
  and and_25 (and_25_out, not_41_out, not_42_out, c);
  and and_26 (and_26_out, not_43_out, c, not_44_out);
  and and_27 (and_27_out, not_45_out, b, not_46_out, d);
  and and_28 (and_28_out, a, not_47_out, not_48_out);
  or or_6 (s, and_19_out, and_20_out, and_21_out);
  or or_7 (t, and_22_out, and_23_out);
  or or_8 (w, and_24_out, and_25_out, and_26_out, and_27_out, and_28_out);
endmodule

module Contagem (
  input  Play,
  input  Pause,
  input  [7:0] Horas,
  input  [7:0] Minutos,
  input  [7:0] Segundos,
  output Ativo,
  output Hora,
  output Minuto,
  output Segundo
);

  wire clock_1_out, comparatodos_1_out_4, comparator_1_eq, comparator_2_eq, nor_1_out, not_1_out, or_1_out,
       transistor_1_out;

  D_Flip_Flop d_ff_1 (.clk(Play), .D(Play), .Q(Ativo), .reset(or_1_out));  // open: Qn, preset, en
  or or_1 (or_1_out, Pause, comparatodos_1_out_4);
  Comparator comparator_1 (.a(Minutos), .b(8'h3b), .eq(comparator_1_eq));  // open: gt, lt
  Comparator comparator_2 (.a(Segundos), .b(8'h3b), .eq(comparator_2_eq));  // open: gt, lt
  Transistor #(.\type ("n")) transistor_1 (.in(clock_1_out), .out(transistor_1_out), .gate(Ativo));
  Pull_Resistor pull_resistor_1 (.node(transistor_1_out));
  Clock clock_1 (.out(clock_1_out));
  ComparaTodos comparatodos_1 (.Horas(Horas), .Minutos(Minutos), .Segundos(Segundos), .out_4(comparatodos_1_out_4));
  not not_1 (not_1_out, Ativo);
  nor nor_1 (nor_1_out, not_1_out, comparatodos_1_out_4);
  Transistor #(.\type ("n")) transistor_2 (.in(comparator_1_eq), .out(Hora), .gate(nor_1_out));
  Pull_Resistor pull_resistor_2 (.node(Hora));
  Transistor #(.\type ("n")) transistor_3 (.in(comparator_2_eq), .out(Minuto), .gate(nor_1_out));
  Pull_Resistor pull_resistor_3 (.node(Minuto));
  Transistor #(.\type ("n")) transistor_4 (.in(transistor_1_out), .out(Segundo), .gate(nor_1_out));
  Pull_Resistor pull_resistor_4 (.node(Segundo));
endmodule

module Adiciona (
  input  Somar,
  input  Ativador,
  input  Zerar,
  input  [7:0] ValorMaximo,
  output [7:0] Saida_8Bits,
  output [3:0] SaidaA,
  output [3:0] SaidaB
);

  wire and_1_out, comparator_1_eq, comparator_1_gt, comparator_2_gt, not_1_out, or_1_out, or_2_out;
  wire [7:0] adder_1_out, bit_extender_1_out, bit_extender_2_out, chave_1_saida_8bits, chave_2_saida_8bits,
       subtractor_1_out, subtractor_2_out;

  and and_1 (and_1_out, 1'b1, not_1_out);
  not not_1 (not_1_out, Ativador);
  assign bit_extender_1_out = {{7{1'b0}}, and_1_out};  // Bit_Extender bit_extender_1
  assign bit_extender_2_out = {{7{1'b0}}, Ativador};  // Bit_Extender bit_extender_2
  Adder adder_1 (.a(Saida_8Bits), .b(bit_extender_1_out), .out(adder_1_out));  // open: cin, cout
  Subtractor subtractor_1 (.a(Saida_8Bits), .b(bit_extender_2_out), .out(subtractor_1_out));  // open: bin, bout
  Chave chave_1 (
    .Entrada_A(adder_1_out), .Entrada_B(subtractor_1_out), .Chave(and_1_out),
    .Saida_8Bits(chave_1_saida_8bits));
  Subtractor subtractor_2 (.a(ValorMaximo), .b(8'h1), .out(subtractor_2_out));  // open: bin, bout
  Comparator comparator_1 (
    .a(chave_1_saida_8bits), .b({8{1'b0}}), .gt(comparator_1_gt), .eq(comparator_1_eq));  // open: lt
  Comparator comparator_2 (.a(chave_1_saida_8bits), .b(ValorMaximo), .gt(comparator_2_gt));  // open: eq, lt
  Chave chave_2 (
    .Entrada_A(chave_1_saida_8bits), .Entrada_B(subtractor_2_out), .Chave(or_1_out),
    .Saida_8Bits(chave_2_saida_8bits));
  or or_1 (or_1_out, comparator_1_gt, comparator_1_eq);
  Register Acumulador (.D(chave_2_saida_8bits), .Q(Saida_8Bits), .clk(Somar), .clr(or_2_out));  // open: en
  or or_2 (or_2_out, comparator_2_gt, Zerar);
  ConvTime convtime_1 (.Entrada_de_8Bits(Saida_8Bits), .SaidaA(SaidaA), .SaidaB(SaidaB));
endmodule

module ConvTime (
  input  [7:0] Entrada_de_8Bits,
  output [3:0] SaidaA,
  output [3:0] SaidaB
);

  wire [5:0] bit_extender_1_out;

  Bit_Extender #(.out_width(6)) bit_extender_1 (.in(Entrada_de_8Bits), .out(bit_extender_1_out));
  Conv conv_1 (
    .a(bit_extender_1_out[5]), .b(bit_extender_1_out[4]), .c(bit_extender_1_out[3]),
    .d(bit_extender_1_out[2]), .e(bit_extender_1_out[1]), .f(bit_extender_1_out[0]), .x(SaidaA[3]),
    .y(SaidaA[2]), .z(SaidaA[1]), .u(SaidaA[0]), .v(SaidaB[3]), .w(SaidaB[2]), .s(SaidaB[1]), .t(SaidaB[0]));
endmodule

module Conv (
  input  a,
  input  b,
  input  c,
  input  d,
  input  e,
  input  f,
  output x,
  output y,
  output z,
  output u,
  output v,
  output w,
  output s,
  output t
);

  wire and_1_out, and_2_out, and_3_out, and_4_out, and_5_out, and_6_out, and_7_out, and_8_out, and_9_out,
       and_10_out, and_11_out, and_12_out, and_13_out, and_14_out, and_15_out, and_16_out, and_17_out,
       and_18_out, and_19_out, and_20_out, and_21_out, and_22_out, and_23_out, and_24_out, and_25_out,
       and_26_out, and_27_out, and_28_out, and_29_out, and_30_out, and_31_out, and_32_out, and_33_out,
       and_34_out, and_35_out, and_36_out, and_37_out, and_38_out, and_39_out, not_1_out, not_2_out,
       not_3_out, not_4_out, not_5_out, not_6_out, not_7_out, not_8_out, not_9_out, not_10_out, not_11_out,
       not_12_out, not_13_out, not_14_out, not_15_out, not_16_out, not_17_out, not_18_out, not_19_out,
       not_20_out, not_21_out, not_22_out, not_23_out, not_24_out, not_25_out, not_26_out, not_27_out,
       not_28_out, not_29_out, not_30_out, not_31_out, not_32_out, not_33_out, not_34_out, not_35_out,
       not_36_out, not_37_out, not_38_out, not_39_out, not_40_out, not_41_out, not_42_out, not_43_out,
       not_44_out, not_45_out, not_46_out, not_47_out, not_48_out, not_49_out, not_50_out, not_51_out,
       not_52_out, not_53_out, not_54_out, not_55_out, not_56_out, not_57_out, not_58_out, not_59_out,
       not_60_out, not_61_out, not_62_out, not_63_out, not_64_out, not_65_out, not_66_out, not_67_out,
       not_68_out, not_69_out, not_70_out, not_71_out, not_72_out, not_73_out;

  and and_1 (and_1_out, a, c);
  and and_2 (and_2_out, a, b);
  not not_1 (not_1_out, a);
  not not_2 (not_2_out, a);
  not not_3 (not_3_out, b);
  not not_4 (not_4_out, c);
  not not_5 (not_5_out, a);
  not not_6 (not_6_out, b);
  not not_7 (not_7_out, a);
  not not_8 (not_8_out, b);
  not not_9 (not_9_out, a);
  not not_10 (not_10_out, a);
  not not_11 (not_11_out, c);
  not not_12 (not_12_out, d);
  not not_13 (not_13_out, b);
  not not_14 (not_14_out, c);
  not not_15 (not_15_out, c);
  not not_16 (not_16_out, c);
  not not_17 (not_17_out, d);
  not not_18 (not_18_out, a);
  not not_19 (not_19_out, b);
  not not_20 (not_20_out, d);
  not not_21 (not_21_out, e);
  not not_22 (not_22_out, a);
  not not_23 (not_23_out, c);
  not not_24 (not_24_out, d);
  not not_25 (not_25_out, a);
  not not_26 (not_26_out, e);
  not not_27 (not_27_out, b);
  not not_28 (not_28_out, c);
  not not_29 (not_29_out, c);
  not not_30 (not_30_out, d);
  not not_31 (not_31_out, e);
  not not_32 (not_32_out, d);
  not not_33 (not_33_out, a);
  not not_34 (not_34_out, b);
  not not_35 (not_35_out, c);
  not not_36 (not_36_out, b);
  not not_37 (not_37_out, c);
  not not_38 (not_38_out, e);
  not not_39 (not_39_out, b);
  not not_40 (not_40_out, a);
  not not_41 (not_41_out, d);
  not not_42 (not_42_out, e);
  not not_43 (not_43_out, a);
  not not_44 (not_44_out, d);
  not not_45 (not_45_out, d);
  not not_46 (not_46_out, e);
  not not_47 (not_47_out, b);
  not not_48 (not_48_out, c);
  not not_49 (not_49_out, d);
  not not_50 (not_50_out, b);
  not not_51 (not_51_out, c);
  not not_52 (not_52_out, a);
  not not_53 (not_53_out, b);
  not not_54 (not_54_out, c);
  not not_55 (not_55_out, a);
  not not_56 (not_56_out, c);
  not not_57 (not_57_out, a);
  not not_58 (not_58_out, b);
  not not_59 (not_59_out, e);
  not not_60 (not_60_out, a);
  not not_61 (not_61_out, c);
  not not_62 (not_62_out, d);
  not not_63 (not_63_out, e);
  not not_64 (not_64_out, a);
  not not_65 (not_65_out, d);
  not not_66 (not_66_out, b);
  not not_67 (not_67_out, c);
  not not_68 (not_68_out, e);
  not not_69 (not_69_out, c);
  not not_70 (not_70_out, e);
  not not_71 (not_71_out, b);
  not not_72 (not_72_out, d);
  not not_73 (not_73_out, e);
  or or_1 (y, and_1_out, and_2_out);
  and and_3 (and_3_out, not_1_out, b, d);
  and and_4 (and_4_out, not_2_out, b, c);
  and and_5 (and_5_out, b, c, d);
  and and_6 (and_6_out, a, not_3_out, not_4_out);
  and and_7 (and_7_out, not_5_out, not_6_out, c, e);
  and and_8 (and_8_out, not_7_out, not_8_out, c, d);
  and and_9 (and_9_out, not_9_out, c, d, e);
  and and_10 (and_10_out, not_10_out, b, not_11_out, not_12_out);
  and and_11 (and_11_out, a, not_13_out, not_14_out);
  and and_12 (and_12_out, a, not_15_out, e);
  and and_13 (and_13_out, a, not_16_out, d);
  and and_14 (and_14_out, a, b, c, not_17_out);
  and and_15 (and_15_out, not_18_out, not_19_out, c, not_20_out, not_21_out);
  and and_16 (and_16_out, not_22_out, b, not_23_out, not_24_out, e);
  and and_17 (and_17_out, not_25_out, b, c, d, not_26_out);
  and and_18 (and_18_out, a, not_27_out, not_28_out, d, e);
  and and_19 (and_19_out, a, b, not_29_out, not_30_out, not_31_out);
  and and_20 (and_20_out, a, b, c, not_32_out, e);
  and and_21 (and_21_out, not_33_out, not_34_out, not_35_out, d);
  and and_22 (and_22_out, not_36_out, not_37_out, d, not_38_out);
  and and_23 (and_23_out, not_39_out, c, d, e);
  and and_24 (and_24_out, not_40_out, b, not_41_out, not_42_out);
  and and_25 (and_25_out, not_43_out, b, c, not_44_out);
  and and_26 (and_26_out, b, c, not_45_out, not_46_out);
  and and_27 (and_27_out, a, not_47_out, not_48_out, not_49_out, e);
  and and_28 (and_28_out, a, not_50_out, c, d);
  and and_29 (and_29_out, a, b, not_51_out, d, e);
  and and_30 (and_30_out, not_52_out, not_53_out, not_54_out, e);
  and and_31 (and_31_out, not_55_out, not_56_out, d, e);
  and and_32 (and_32_out, not_57_out, not_58_out, c, d, not_59_out);
  and and_33 (and_33_out, not_60_out, b, not_61_out, not_62_out, not_63_out);
  and and_34 (and_34_out, not_64_out, b, c, not_65_out, e);
  and and_35 (and_35_out, a, not_66_out, not_67_out, not_68_out);
  and and_36 (and_36_out, a, not_69_out, d, not_70_out);
  and and_37 (and_37_out, a, not_71_out, c, e);
  and and_38 (and_38_out, a, c, d, e);
  and and_39 (and_39_out, a, b, c, not_72_out, not_73_out);
  or or_2 (z, and_3_out, and_4_out, and_5_out, and_6_out);
  or or_3 (u, and_7_out, and_8_out, and_9_out, and_10_out, and_11_out, and_12_out, and_13_out, and_14_out);
  or or_4 (v, and_15_out, and_16_out, and_17_out, and_18_out, and_19_out, and_20_out);
  or or_5 (w, and_21_out, and_22_out, and_23_out, and_24_out, and_25_out, and_26_out, and_27_out, and_28_out, and_29_out);
  or or_6 (s, and_30_out, and_31_out, and_32_out, and_33_out, and_34_out, and_35_out, and_36_out, and_37_out, and_38_out, and_39_out);

  assign t = f;
  assign x = 1'b0;
endmodule

module Chave (
  input  [7:0] Entrada_A,
  input  [7:0] Entrada_B,
  input  Chave,
  output [7:0] Saida_8Bits
);

  wire not_1_out;
  wire [7:0] transistor_1_out, transistor_2_out;

  Transistor #(.\type ("n"), .width(8)) transistor_1 (.in(Entrada_A), .out(transistor_1_out), .gate(Chave));
  Transistor #(.\type ("n"), .width(8)) transistor_2 (.in(Entrada_B), .out(transistor_2_out), .gate(not_1_out));
  Pull_Resistor pull_resistor_1 (.node(transistor_1_out));
  Pull_Resistor pull_resistor_2 (.node(transistor_2_out));
  not not_1 (not_1_out, Chave);
  Adder adder_1 (.a(transistor_1_out), .b(transistor_2_out), .out(Saida_8Bits));  // open: cin, cout
endmodule

// VerificaZerado
module ComparaTodos (
  input  [7:0] Horas,
  input  [7:0] Minutos,
  input  [7:0] Segundos,
  output out_4
);

  wire comparator_1_eq, comparator_2_eq, comparator_3_eq;

  Comparator comparator_1 (.a(Horas), .b({8{1'b0}}), .eq(comparator_1_eq));  // open: gt, lt
  Comparator comparator_2 (.a(Minutos), .b({8{1'b0}}), .eq(comparator_2_eq));  // open: gt, lt
  Comparator comparator_3 (.a(Segundos), .b({8{1'b0}}), .eq(comparator_3_eq));  // open: gt, lt
  and and_1 (out_4, comparator_1_eq, comparator_2_eq, comparator_3_eq);
endmodule
