// Logisim project Relogio.circ as structural Verilog: 7 circuits, main circuit main
module main (
  input  Somar
);

  wire Add_2_out, Add_3_out, Add_out, controler_1_hora, controler_1_minuto, controler_1_segundo, led_1_s,
       led_1_t, led_1_u, led_1_v, led_1_w, led_1_x, led_1_y, led_1_z, led_2_s, led_2_t, led_2_u, led_2_v,
       led_2_w, led_2_x, led_2_y, led_2_z, led_3_s, led_3_t, led_3_u, led_3_v, led_3_w, led_3_x, led_3_y,
       led_3_z, led_4_s, led_4_t, led_4_u, led_4_v, led_4_w, led_4_x, led_4_y, led_4_z, led_5_s, led_5_t,
       led_5_u, led_5_v, led_5_w, led_5_x, led_5_y, led_5_z, led_6_s, led_6_t, led_6_u, led_6_v, led_6_w,
       led_6_x, led_6_y, led_6_z, or_1_out, or_2_out, or_3_out, Pause_out, Play_out, Zerar_out;
  wire [3:0] convert_1_out_2, convert_1_out_3, convert_2_out_2, convert_2_out_3, convert_3_out_2,
       convert_3_out_3;
  wire [7:0] soma_1_saida, soma_2_saida, soma_3_saida;

  Led led_1 (
    .a(convert_1_out_2[3]), .b(convert_1_out_2[2]), .c(convert_1_out_2[1]), .d(convert_1_out_2[0]),
    .x(led_1_x), .y(led_1_y), .z(led_1_z), .u(led_1_u), .v(led_1_v), .w(led_1_w), .s(led_1_s), .t(led_1_t));
  _7_Segment_Display u_7_segment_display_1 (
    .g(led_1_u), .f(led_1_z), .a(led_1_y), .b(led_1_x), .e(led_1_v), .d(led_1_w), .c(led_1_s), .dp(led_1_t));
  Led led_2 (
    .a(convert_1_out_3[3]), .b(convert_1_out_3[2]), .c(convert_1_out_3[1]), .d(convert_1_out_3[0]),
    .x(led_2_x), .y(led_2_y), .z(led_2_z), .u(led_2_u), .v(led_2_v), .w(led_2_w), .s(led_2_s), .t(led_2_t));
  or or_1 (or_1_out, controler_1_hora, Add_out);
  Button Add (.out(Add_out));
  _7_Segment_Display u_7_segment_display_2 (
    .g(led_2_u), .f(led_2_z), .a(led_2_y), .b(led_2_x), .e(led_2_v), .d(led_2_w), .c(led_2_s), .dp(led_2_t));
  Convert convert_1 (.in_1(soma_1_saida), .out_2(convert_1_out_2), .out_3(convert_1_out_3));
  Soma soma_1 (
    .Maximo(8'h18), .Subtrair(Somar), .Saida(soma_1_saida), .Zerar(Zerar_out), .Pulso_Soma(or_1_out));  // open: Vai_Um, Pausar
  Led led_3 (
    .a(convert_2_out_2[3]), .b(convert_2_out_2[2]), .c(convert_2_out_2[1]), .d(convert_2_out_2[0]),
    .x(led_3_x), .y(led_3_y), .z(led_3_z), .u(led_3_u), .v(led_3_v), .w(led_3_w), .s(led_3_s), .t(led_3_t));
  Button Play (.out(Play_out));
  _7_Segment_Display u_7_segment_display_3 (
    .g(led_3_u), .f(led_3_z), .a(led_3_y), .b(led_3_x), .e(led_3_v), .d(led_3_w), .c(led_3_s), .dp(led_3_t));
  Led led_4 (
    .a(convert_2_out_3[3]), .b(convert_2_out_3[2]), .c(convert_2_out_3[1]), .d(convert_2_out_3[0]),
    .x(led_4_x), .y(led_4_y), .z(led_4_z), .u(led_4_u), .v(led_4_v), .w(led_4_w), .s(led_4_s), .t(led_4_t));
  Convert convert_2 (.in_1(soma_2_saida), .out_2(convert_2_out_2), .out_3(convert_2_out_3));
  or or_2 (or_2_out, controler_1_minuto, Add_2_out);
  Button Add_2 (.out(Add_2_out));
  Controler controler_1 (
    .Play(Play_out), .Pause(Pause_out), .Horas(soma_1_saida), .Somar(Somar), .Minutos(soma_2_saida),
    .Segundos(soma_3_saida), .Hora(controler_1_hora), .Minuto(controler_1_minuto),
    .Segundo(controler_1_segundo));
  Button Pause (.out(Pause_out));
  _7_Segment_Display u_7_segment_display_4 (
    .g(led_4_u), .f(led_4_z), .a(led_4_y), .b(led_4_x), .e(led_4_v), .d(led_4_w), .c(led_4_s), .dp(led_4_t));
  Soma soma_2 (
    .Maximo(8'h3c), .Subtrair(Somar), .Saida(soma_2_saida), .Zerar(Zerar_out), .Pulso_Soma(or_2_out));  // open: Vai_Um, Pausar
  _7_Segment_Display u_7_segment_display_5 (
    .g(led_5_u), .f(led_5_z), .a(led_5_y), .b(led_5_x), .e(led_5_v), .d(led_5_w), .c(led_5_s), .dp(led_5_t));
  Led led_5 (
    .a(convert_3_out_2[3]), .b(convert_3_out_2[2]), .c(convert_3_out_2[1]), .d(convert_3_out_2[0]),
    .x(led_5_x), .y(led_5_y), .z(led_5_z), .u(led_5_u), .v(led_5_v), .w(led_5_w), .s(led_5_s), .t(led_5_t));
  _7_Segment_Display u_7_segment_display_6 (
    .g(led_6_u), .f(led_6_z), .a(led_6_y), .b(led_6_x), .e(led_6_v), .d(led_6_w), .c(led_6_s), .dp(led_6_t));
  Led led_6 (
    .a(convert_3_out_3[3]), .b(convert_3_out_3[2]), .c(convert_3_out_3[1]), .d(convert_3_out_3[0]),
    .x(led_6_x), .y(led_6_y), .z(led_6_z), .u(led_6_u), .v(led_6_v), .w(led_6_w), .s(led_6_s), .t(led_6_t));
  Convert convert_3 (.in_1(soma_3_saida), .out_2(convert_3_out_2), .out_3(convert_3_out_3));
  or or_3 (or_3_out, controler_1_segundo, Add_3_out);
  Button Add_3 (.out(Add_3_out));
  Soma soma_3 (
    .Maximo(8'h3c), .Subtrair(Somar), .Saida(soma_3_saida), .Zerar(Zerar_out), .Pulso_Soma(or_3_out));  // open: Vai_Um, Pausar
  Button Zerar (.out(Zerar_out));

  // Notes on the sheet:
  //   :
  //   :
endmodule

module outXout (
  input  [7:0] Primeiro,
  input  Flag,
  input  [7:0] Segundo,
  output [7:0] Saida
);

  Transistor #(.gate("br"), .width(8)) transistor_1 (.in(Primeiro), .out(Saida), .gate(Flag));
  Transistor #(.\type ("n"), .width(8)) transistor_2 (.in(Segundo), .out(Saida), .gate(Flag));
  Pull_Resistor pull_resistor_1 (.node(Saida));
endmodule

module Soma (
  input  [7:0] Maximo,
  input  Subtrair,
  input  Pausar,
  input  Zerar,
  input  Pulso_Soma,
  output Vai_Um,
  output [7:0] Saida
);

  wire bit_extender_1_out, comparator_1_lt, comparator_2_gt, comparator_2_lt, not_1_out, not_2_out,
       not_3_out, or_1_out, or_2_out;
  wire [7:0] adder_1_out, bit_extender_2_out, bit_extender_3_out, outxout_2_saida, outxout_3_saida,
       outxout_4_saida, register_1_q, subtractor_1_out, subtractor_2_out, transistor_1_out;

  Transistor #(.\type ("n"), .gate("br"), .width(8)) transistor_1 (
    .in(outxout_3_saida), .out(transistor_1_out), .gate(bit_extender_1_out));
  Pull_Resistor pull_resistor_1 (.node(transistor_1_out));
  outXout outxout_1 (.Flag(Pausar), .Primeiro(transistor_1_out), .Segundo(Saida), .Saida(Saida));
  not not_1 (not_1_out, bit_extender_1_out);
  Pull_Resistor pull_resistor_2 (.node(Pausar));
  Bit_Extender #(.out_width(1)) bit_extender_1 (.in(outxout_2_saida), .out(bit_extender_1_out));
  outXout outxout_2 (
    .Flag(not_3_out), .Primeiro(bit_extender_2_out), .Segundo(bit_extender_3_out), .Saida(outxout_2_saida));
  and and_1 (Vai_Um, not_1_out, not_2_out);
  not not_2 (not_2_out, Zerar);
  outXout outxout_3 (
    .Flag(comparator_2_lt), .Primeiro(register_1_q), .Segundo(subtractor_1_out), .Saida(outxout_3_saida));
  Subtractor subtractor_1 (.a(Maximo), .b(8'h1), .out(subtractor_1_out));  // open: bin, bout
  not not_3 (not_3_out, Subtrair);
  Subtractor subtractor_2 (.a(Saida), .b(8'h1), .out(subtractor_2_out));  // open: bin, bout
  Adder adder_1 (.a(Saida), .b(8'h1), .out(adder_1_out));  // open: cin, cout
  assign bit_extender_2_out = {{7{1'b0}}, comparator_1_lt};  // Bit_Extender bit_extender_2
  outXout outxout_4 (.Flag(not_3_out), .Primeiro(adder_1_out), .Segundo(subtractor_2_out), .Saida(outxout_4_saida));
  Comparator comparator_1 (.a(register_1_q), .b(Maximo), .lt(comparator_1_lt));  // open: gt, eq
  Comparator comparator_2 (.a(register_1_q), .b({8{1'b0}}), .gt(comparator_2_gt), .lt(comparator_2_lt));  // open: eq
  assign bit_extender_3_out = {{7{1'b0}}, or_2_out};  // Bit_Extender bit_extender_3
  or or_1 (or_1_out, Pulso_Soma, Zerar);
  or or_2 (or_2_out, comparator_2_lt, comparator_2_gt);
  Register register_1 (.D(outxout_4_saida), .Q(register_1_q), .clk(or_1_out), .clr(Zerar));  // open: en
endmodule

module Led (
  input  a,
  input  b,
  input  c,
  input  d,
  output x,
  output y,
  output z,
  output u,
  output v,
  output w,
  output s,
  output t
);

  wire and_1_out, and_2_out, and_3_out, and_4_out, and_5_out, and_6_out, and_7_out, and_8_out, and_9_out,
       and_10_out, and_11_out, and_12_out, and_13_out, and_14_out, and_15_out, and_16_out, and_17_out,
       and_18_out, and_19_out, and_20_out, and_21_out, and_22_out, and_23_out, and_24_out, and_25_out,
       and_26_out, and_27_out, and_28_out, not_1_out, not_2_out, not_3_out, not_4_out, not_5_out, not_6_out,
       not_7_out, not_8_out, not_9_out, not_10_out, not_11_out, not_12_out, not_13_out, not_14_out,
       not_15_out, not_16_out, not_17_out, not_18_out, not_19_out, not_20_out, not_21_out, not_22_out,
       not_23_out, not_24_out, not_25_out, not_26_out, not_27_out, not_28_out, not_29_out, not_30_out,
       not_31_out, not_32_out, not_33_out, not_34_out, not_35_out, not_36_out, not_37_out, not_38_out,
       not_39_out, not_40_out, not_41_out, not_42_out, not_43_out, not_44_out, not_45_out, not_46_out,
       not_47_out, not_48_out, not_49_out, not_50_out, not_51_out, not_52_out;

  not not_1 (not_1_out, a);
  and and_1 (and_1_out, not_1_out, not_2_out);
  not not_2 (not_2_out, b);
  not not_3 (not_3_out, a);
  and and_2 (and_2_out, not_3_out, not_4_out, not_5_out);
  not not_4 (not_4_out, c);
  not not_5 (not_5_out, d);
  not not_6 (not_6_out, b);
  and and_3 (and_3_out, not_6_out, not_7_out);
  not not_7 (not_7_out, c);
  not not_8 (not_8_out, a);
  and and_4 (and_4_out, not_8_out, c, d);
  not not_9 (not_9_out, a);
  and and_5 (and_5_out, not_9_out, not_10_out, not_11_out);
  not not_10 (not_10_out, b);
  not not_11 (not_11_out, d);
  not not_12 (not_12_out, a);
  and and_6 (and_6_out, not_12_out, c);
  not not_13 (not_13_out, a);
  and and_7 (and_7_out, not_13_out, b, d);
  and and_8 (and_8_out, a, not_14_out, not_15_out);
  not not_14 (not_14_out, b);
  not not_15 (not_15_out, c);
  not not_16 (not_16_out, a);
  and and_9 (and_9_out, not_16_out, not_17_out, not_18_out);
  not not_17 (not_17_out, c);
  not not_18 (not_18_out, d);
  not not_19 (not_19_out, a);
  and and_10 (and_10_out, not_19_out, b, not_20_out);
  not not_20 (not_20_out, c);
  not not_21 (not_21_out, a);
  and and_11 (and_11_out, not_21_out, b, not_22_out);
  not not_22 (not_22_out, d);
  and and_12 (and_12_out, a, not_23_out, not_24_out);
  not not_23 (not_23_out, b);
  not not_24 (not_24_out, c);
  not not_25 (not_25_out, a);
  and and_13 (and_13_out, not_25_out, not_26_out, c);
  not not_26 (not_26_out, b);
  not not_27 (not_27_out, a);
  and and_14 (and_14_out, not_27_out, b, not_28_out);
  not not_28 (not_28_out, c);
  not not_29 (not_29_out, a);
  and and_15 (and_15_out, not_29_out, b, not_30_out);
  not not_30 (not_30_out, d);
  not not_31 (not_31_out, b);
  and and_16 (and_16_out, a, not_31_out, not_32_out);
  not not_32 (not_32_out, c);
  not not_33 (not_33_out, b);
  and and_17 (and_17_out, not_33_out, not_34_out, not_35_out);
  not not_34 (not_34_out, c);
  not not_35 (not_35_out, d);
  not not_36 (not_36_out, a);
  and and_18 (and_18_out, not_36_out, c, not_37_out);
  not not_37 (not_37_out, d);
  not not_38 (not_38_out, a);
  not not_39 (not_39_out, b);
  not not_40 (not_40_out, d);
  not not_41 (not_41_out, a);
  not not_42 (not_42_out, b);
  not not_43 (not_43_out, a);
  not not_44 (not_44_out, d);
  not not_45 (not_45_out, a);
  not not_46 (not_46_out, c);
  not not_47 (not_47_out, b);
  not not_48 (not_48_out, c);
  not not_49 (not_49_out, b);
  and and_19 (and_19_out, not_49_out, not_50_out);
  not not_50 (not_50_out, c);
  not not_51 (not_51_out, a);
  and and_20 (and_20_out, not_51_out, d);
  not not_52 (not_52_out, a);
  and and_21 (and_21_out, not_52_out, b);
  and and_22 (and_22_out, a, c);
  and and_23 (and_23_out, a, b);
  or or_1 (x, and_1_out, and_2_out, and_3_out, and_4_out);
  or or_2 (y, and_5_out, and_6_out, and_7_out, and_8_out);
  or or_3 (z, and_9_out, and_10_out, and_11_out, and_12_out);
  or or_4 (u, and_13_out, and_14_out, and_15_out, and_16_out);
  or or_5 (v, and_17_out, and_18_out);
  and and_24 (and_24_out, not_38_out, not_39_out, not_40_out);
  and and_25 (and_25_out, not_41_out, not_42_out, c);
  and and_26 (and_26_out, not_43_out, c, not_44_out);
  and and_27 (and_27_out, not_45_out, b, not_46_out, d);
  and and_28 (and_28_out, a, not_47_out, not_48_out);
  or or_6 (s, and_19_out, and_20_out, and_21_out);
  or or_7 (t, and_22_out, and_23_out);
  or or_8 (w, and_24_out, and_25_out, and_26_out, and_27_out, and_28_out);
endmodule

module Convert (
  input  [7:0] in_1,
  output [3:0] out_2,
  output [3:0] out_3
);

  wire [5:0] bit_extender_1_out;

  Bit_Extender #(.out_width(6)) bit_extender_1 (.in(in_1), .out(bit_extender_1_out));
  Inteiro2Time inteiro2time_1 (
    .a(bit_extender_1_out[5]), .b(bit_extender_1_out[4]), .c(bit_extender_1_out[3]),
    .d(bit_extender_1_out[2]), .e(bit_extender_1_out[1]), .f(bit_extender_1_out[0]), .x(out_2[3]),
    .y(out_2[2]), .z(out_2[1]), .u(out_2[0]), .v(out_3[3]), .w(out_3[2]), .s(out_3[1]), .t(out_3[0]));
endmodule

module Inteiro2Time (
  input  a,
  input  b,
  input  c,
  input  d,
  input  e,
  input  f,
  output x,
  output y,
  output z,
  output u,
  output v,
  output w,
  output s,
  output t
);

  wire and_1_out, and_2_out, and_3_out, and_4_out, and_5_out, and_6_out, and_7_out, and_8_out, and_9_out,
       and_10_out, and_11_out, and_12_out, and_13_out, and_14_out, and_15_out, and_16_out, and_17_out,
       and_18_out, and_19_out, and_20_out, and_21_out, and_22_out, and_23_out, and_24_out, and_25_out,
       and_26_out, and_27_out, and_28_out, and_29_out, and_30_out, and_31_out, and_32_out, and_33_out,
       and_34_out, and_35_out, and_36_out, and_37_out, and_38_out, and_39_out, not_1_out, not_2_out,
       not_3_out, not_4_out, not_5_out, not_6_out, not_7_out, not_8_out, not_9_out, not_10_out, not_11_out,
       not_12_out, not_13_out, not_14_out, not_15_out, not_16_out, not_17_out, not_18_out, not_19_out,
       not_20_out, not_21_out, not_22_out, not_23_out, not_24_out, not_25_out, not_26_out, not_27_out,
       not_28_out, not_29_out, not_30_out, not_31_out, not_32_out, not_33_out, not_34_out, not_35_out,
       not_36_out, not_37_out, not_38_out, not_39_out, not_40_out, not_41_out, not_42_out, not_43_out,
       not_44_out, not_45_out, not_46_out, not_47_out, not_48_out, not_49_out, not_50_out, not_51_out,
       not_52_out, not_53_out, not_54_out, not_55_out, not_56_out, not_57_out, not_58_out, not_59_out,
       not_60_out, not_61_out, not_62_out, not_63_out, not_64_out, not_65_out, not_66_out, not_67_out,
       not_68_out, not_69_out, not_70_out, not_71_out, not_72_out, not_73_out;

  and and_1 (and_1_out, a, c);
  and and_2 (and_2_out, a, b);
  not not_1 (not_1_out, a);
  not not_2 (not_2_out, a);
  not not_3 (not_3_out, b);
  not not_4 (not_4_out, c);
  not not_5 (not_5_out, a);
  not not_6 (not_6_out, b);
  not not_7 (not_7_out, a);
  not not_8 (not_8_out, b);
  not not_9 (not_9_out, a);
  not not_10 (not_10_out, a);
  not not_11 (not_11_out, c);
  not not_12 (not_12_out, d);
  not not_13 (not_13_out, b);
  not not_14 (not_14_out, c);
  not not_15 (not_15_out, c);
  not not_16 (not_16_out, c);
  not not_17 (not_17_out, d);
  not not_18 (not_18_out, a);
  not not_19 (not_19_out, b);
  not not_20 (not_20_out, d);
  not not_21 (not_21_out, e);
  not not_22 (not_22_out, a);
  not not_23 (not_23_out, c);
  not not_24 (not_24_out, d);
  not not_25 (not_25_out, a);
  not not_26 (not_26_out, e);
  not not_27 (not_27_out, b);
  not not_28 (not_28_out, c);
  not not_29 (not_29_out, c);
  not not_30 (not_30_out, d);
  not not_31 (not_31_out, e);
  not not_32 (not_32_out, d);
  not not_33 (not_33_out, a);
  not not_34 (not_34_out, b);
  not not_35 (not_35_out, c);
  not not_36 (not_36_out, b);
  not not_37 (not_37_out, c);
  not not_38 (not_38_out, e);
  not not_39 (not_39_out, b);
  not not_40 (not_40_out, a);
  not not_41 (not_41_out, d);
  not not_42 (not_42_out, e);
  not not_43 (not_43_out, a);
  not not_44 (not_44_out, d);
  not not_45 (not_45_out, d);
  not not_46 (not_46_out, e);
  not not_47 (not_47_out, b);
  not not_48 (not_48_out, c);
  not not_49 (not_49_out, d);
  not not_50 (not_50_out, b);
  not not_51 (not_51_out, c);
  not not_52 (not_52_out, a);
  not not_53 (not_53_out, b);
  not not_54 (not_54_out, c);
  not not_55 (not_55_out, a);
  not not_56 (not_56_out, c);
  not not_57 (not_57_out, a);
  not not_58 (not_58_out, b);
  not not_59 (not_59_out, e);
  not not_60 (not_60_out, a);
  not not_61 (not_61_out, c);
  not not_62 (not_62_out, d);
  not not_63 (not_63_out, e);
  not not_64 (not_64_out, a);
  not not_65 (not_65_out, d);
  not not_66 (not_66_out, b);
  not not_67 (not_67_out, c);
  not not_68 (not_68_out, e);
  not not_69 (not_69_out, c);
  not not_70 (not_70_out, e);
  not not_71 (not_71_out, b);
  not not_72 (not_72_out, d);
  not not_73 (not_73_out, e);
  or or_1 (y, and_1_out, and_2_out);
  and and_3 (and_3_out, not_1_out, b, d);
  and and_4 (and_4_out, not_2_out, b, c);
  and and_5 (and_5_out, b, c, d);
  and and_6 (and_6_out, a, not_3_out, not_4_out);
  and and_7 (and_7_out, not_5_out, not_6_out, c, e);
  and and_8 (and_8_out, not_7_out, not_8_out, c, d);
  and and_9 (and_9_out, not_9_out, c, d, e);
  and and_10 (and_10_out, not_10_out, b, not_11_out, not_12_out);
  and and_11 (and_11_out, a, not_13_out, not_14_out);
  and and_12 (and_12_out, a, not_15_out, e);
  and and_13 (and_13_out, a, not_16_out, d);
  and and_14 (and_14_out, a, b, c, not_17_out);
  and and_15 (and_15_out, not_18_out, not_19_out, c, not_20_out, not_21_out);
  and and_16 (and_16_out, not_22_out, b, not_23_out, not_24_out, e);
  and and_17 (and_17_out, not_25_out, b, c, d, not_26_out);
  and and_18 (and_18_out, a, not_27_out, not_28_out, d, e);
  and and_19 (and_19_out, a, b, not_29_out, not_30_out, not_31_out);
  and and_20 (and_20_out, a, b, c, not_32_out, e);
  and and_21 (and_21_out, not_33_out, not_34_out, not_35_out, d);
  and and_22 (and_22_out, not_36_out, not_37_out, d, not_38_out);
  and and_23 (and_23_out, not_39_out, c, d, e);
  and and_24 (and_24_out, not_40_out, b, not_41_out, not_42_out);
  and and_25 (and_25_out, not_43_out, b, c, not_44_out);
  and and_26 (and_26_out, b, c, not_45_out, not_46_out);
  and and_27 (and_27_out, a, not_47_out, not_48_out, not_49_out, e);
  and and_28 (and_28_out, a, not_50_out, c, d);
  and and_29 (and_29_out, a, b, not_51_out, d, e);
  and and_30 (and_30_out, not_52_out, not_53_out, not_54_out, e);
  and and_31 (and_31_out, not_55_out, not_56_out, d, e);
  and and_32 (and_32_out, not_57_out, not_58_out, c, d, not_59_out);
  and and_33 (and_33_out, not_60_out, b, not_61_out, not_62_out, not_63_out);
  and and_34 (and_34_out, not_64_out, b, c, not_65_out, e);
  and and_35 (and_35_out, a, not_66_out, not_67_out, not_68_out);
  and and_36 (and_36_out, a, not_69_out, d, not_70_out);
  and and_37 (and_37_out, a, not_71_out, c, e);
  and and_38 (and_38_out, a, c, d, e);
  and and_39 (and_39_out, a, b, c, not_72_out, not_73_out);
  or or_2 (z, and_3_out, and_4_out, and_5_out, and_6_out);
  or or_3 (u, and_7_out, and_8_out, and_9_out, and_10_out, and_11_out, and_12_out, and_13_out, and_14_out);
  or or_4 (v, and_15_out, and_16_out, and_17_out, and_18_out, and_19_out, and_20_out);
  or or_5 (w, and_21_out, and_22_out, and_23_out, and_24_out, and_25_out, and_26_out, and_27_out, and_28_out, and_29_out);
  or or_6 (s, and_30_out, and_31_out, and_32_out, and_33_out, and_34_out, and_35_out, and_36_out, and_37_out, and_38_out, and_39_out);

  assign t = f;
  assign x = 1'b0;
endmodule

module Controler (
  input  Play,
  input  Pause,
  input  [7:0] Horas,
  input  Somar,
  input  [7:0] Minutos,
  input  [7:0] Segundos,
  output Hora,
  output Minuto,
  output Segundo
);

  wire and_1_out, and_2_out, clock_1_out, comparator_1_eq, comparator_2_eq, comparator_3_eq, comparator_4_eq,
       comparator_5_eq, d_ff_1_q, nor_1_out, not_1_out, not_2_out, or_1_out, or_2_out, transistor_1_out;

  D_Flip_Flop d_ff_1 (.clk(Play), .D(Play), .Q(d_ff_1_q), .reset(or_1_out));  // open: Qn, preset, en
  or or_1 (or_1_out, Pause, and_1_out);
  Comparator comparator_1 (.a(Minutos), .b(8'h3b), .eq(comparator_1_eq));  // open: gt, lt
  Comparator comparator_2 (.a(Segundos), .b(8'h3b), .eq(comparator_2_eq));  // open: gt, lt
  Transistor #(.\type ("n")) transistor_1 (.in(clock_1_out), .out(transistor_1_out), .gate(d_ff_1_q));
  Clock clock_1 (.out(clock_1_out));
  Pull_Resistor pull_resistor_1 (.node(transistor_1_out));
  Comparator comparator_3 (.a(Horas), .b({8{1'b0}}), .eq(comparator_3_eq));  // open: gt, lt
  Comparator comparator_4 (.a(Minutos), .b({8{1'b0}}), .eq(comparator_4_eq));  // open: gt, lt
  Comparator comparator_5 (.a(Segundos), .b({8{1'b0}}), .eq(comparator_5_eq));  // open: gt, lt
  and and_1 (and_1_out, and_2_out, not_1_out);
  not not_1 (not_1_out, Somar);
  and and_2 (and_2_out, comparator_3_eq, comparator_4_eq, comparator_5_eq);
  not not_2 (not_2_out, d_ff_1_q);
  nor nor_1 (nor_1_out, not_2_out, and_2_out);
  or or_2 (or_2_out, nor_1_out, Somar);
  Pull_Resistor pull_resistor_2 (.node(Hora));
  Transistor #(.\type ("n")) transistor_2 (.in(comparator_1_eq), .out(Hora), .gate(or_2_out));
  Transistor #(.\type ("n")) transistor_3 (.in(comparator_2_eq), .out(Minuto), .gate(or_2_out));
  Pull_Resistor pull_resistor_3 (.node(Minuto));
  Transistor #(.\type ("n")) transistor_4 (.in(transistor_1_out), .out(Segundo), .gate(or_2_out));
  Pull_Resistor pull_resistor_4 (.node(Segundo));
endmodule
